// Logisim project BitScanForward.circ as structural Verilog: 3 circuits, main circuit main
module main (
  input  [5:0] A,
  input  Habilitar,
  output ZF,
  output [2:0] Indice
);

  BSF bsf_1 (.ZF(ZF), .Indice(Indice), .Entrada(A), .Habilitar(Habilitar));
endmodule

module BSF (
  input  Habilitar,
  input  [5:0] Entrada,
  output ZF,
  output [2:0] Indice
);

  wire and_1_out, and_2_out, and_3_out, and_4_out, and_5_out, nor_1_out, nor_2_out, nor_3_out, nor_4_out,
       nor_5_out, not_1_out;
  wire [2:0] or_1_out;

  nor nor_1 (nor_1_out, Entrada[0], Entrada[1], Entrada[2], Entrada[3], Entrada[4], Entrada[5]);
  and and_1 (and_1_out, Entrada[0], nor_2_out);
  nor nor_2 (nor_2_out, Entrada[1], Entrada[2], Entrada[3], Entrada[4], Entrada[5]);
  and and_2 (and_2_out, Entrada[2], nor_3_out);
  nor nor_3 (nor_3_out, Entrada[3], Entrada[4], Entrada[5]);
  not not_1 (not_1_out, Entrada[5]);
  and and_3 (and_3_out, not_1_out, Entrada[4]);
  and and_4 (and_4_out, Entrada[1], nor_4_out);
  nor nor_4 (nor_4_out, Entrada[5], Entrada[4], Entrada[3], Entrada[2]);
  nor nor_5 (nor_5_out, Entrada[5], Entrada[4]);
  and and_5 (and_5_out, nor_5_out, Entrada[3]);
  or or_1 (or_1_out[0], and_1_out, and_2_out, and_3_out);
  or or_2 (or_1_out[1], and_4_out, and_2_out, Entrada[5]);
  or or_3 (or_1_out[2], and_3_out, and_5_out, Entrada[5]);
  and and_6 (ZF, nor_1_out, Habilitar);
  Habilitar_3bits habilitar_3bits_1 (.Habilitar(Habilitar), .Entrada(or_1_out), .Salida(Indice));
endmodule

module Habilitar_3bits (
  input  Habilitar,
  input  [2:0] Entrada,
  output [2:0] Salida
);

  and and_1 (Salida[0], Entrada[0], Habilitar);
  and and_2 (Salida[1], Entrada[1], Habilitar);
  and and_3 (Salida[2], Entrada[2], Habilitar);
endmodule
