// Logisim project TEST.circ as structural Verilog: 1 circuit, main circuit main
module main (
  input  [5:0] A,
  input  Habilitar,
  output ZF,
  output [2:0] Indice
);

  BSF bsf_1 (.ZF(ZF), .Indice(Indice), .Entrada(A), .Habilitar(Habilitar));

  // Notes on the sheet:
  //   Bis Scan Forward
endmodule
