// Logisim project Comparador.circ as structural Verilog: 3 circuits, main circuit main
module main (
  input  [5:0] A,
  input  [5:0] B,
  input  Habilitar,
  output SF,
  output ZF
);

  Comparador comparador_1 (.A(A), .B(B), .Hab(Habilitar), .SF(SF), .ZF(ZF));
endmodule

module Comparador (
  input  [5:0] A,
  input  [5:0] B,
  input  Hab,
  output SF,
  output ZF
);

  ComparadorExt comparadorext_1 (
    .A0(A[5]), .B0(B[5]), .A1(A[4]), .B1(B[4]), .A2(A[3]), .B2(B[3]), .A3(A[2]), .B3(B[2]), .A4(A[1]),
    .B4(B[1]), .A5(A[0]), .B5(B[0]), .in_13(Hab), .SF(SF), .ZF(ZF));

  // Notes on the sheet:
  //   A
  //   B
  //   Habilitadora
endmodule

module ComparadorExt (
  input  A0,
  input  B0,
  input  A1,
  input  B1,
  input  A2,
  input  B2,
  input  A3,
  input  B3,
  input  A4,
  input  B4,
  input  A5,
  input  B5,
  input  in_13,
  output SF,
  output ZF
);

  wire and_1_out, and_2_out, and_3_out, and_4_out, and_5_out, and_6_out, and_7_out, and_8_out, and_9_out,
       and_10_out, and_11_out, and_12_out, and_13_out, and_14_out, and_15_out, and_16_out, and_17_out,
       and_18_out, and_19_out, and_20_out, and_21_out, nor_1_out, nor_2_out, nor_3_out, nor_4_out, nor_5_out,
       nor_6_out, not_1_out, not_2_out, not_3_out, not_4_out, not_5_out, not_6_out, not_7_out, not_8_out,
       not_9_out, not_10_out, not_11_out, not_12_out, or_1_out, or_2_out, or_3_out, or_4_out, or_5_out;

  not not_1 (not_1_out, A0);
  not not_2 (not_2_out, B0);
  not not_3 (not_3_out, A1);
  not not_4 (not_4_out, B1);
  not not_5 (not_5_out, A2);
  not not_6 (not_6_out, B2);
  not not_7 (not_7_out, A3);
  not not_8 (not_8_out, B3);
  not not_9 (not_9_out, A4);
  not not_10 (not_10_out, B4);
  not not_11 (not_11_out, A5);
  not not_12 (not_12_out, B5);
  and and_1 (and_1_out, not_1_out, B0);
  and and_2 (and_2_out, A0, not_2_out);
  and and_3 (and_3_out, not_3_out, B1);
  and and_4 (and_4_out, A1, not_4_out);
  and and_5 (and_5_out, not_5_out, B2);
  and and_6 (and_6_out, A2, not_6_out);
  and and_7 (and_7_out, not_7_out, B3);
  and and_8 (and_8_out, A3, not_8_out);
  and and_9 (and_9_out, not_9_out, B4);
  and and_10 (and_10_out, A4, not_10_out);
  and and_11 (and_11_out, not_11_out, B5);
  and and_12 (and_12_out, A5, not_12_out);
  nor nor_1 (nor_1_out, and_1_out, and_2_out);
  nor nor_2 (nor_2_out, and_3_out, and_4_out);
  nor nor_3 (nor_3_out, and_5_out, and_6_out);
  nor nor_4 (nor_4_out, and_7_out, and_8_out);
  nor nor_5 (nor_5_out, and_9_out, and_10_out);
  nor nor_6 (nor_6_out, and_11_out, and_12_out);
  and and_13 (and_13_out, nor_1_out, and_3_out);
  and and_14 (and_14_out, nor_1_out, nor_2_out, and_5_out);
  and and_15 (and_15_out, and_7_out, nor_1_out, nor_2_out, nor_3_out);
  and and_16 (and_16_out, and_9_out, nor_1_out, nor_2_out, nor_3_out);
  and and_17 (and_17_out, and_16_out, nor_4_out);
  and and_18 (and_18_out, and_11_out, nor_1_out, nor_2_out, nor_3_out);
  and and_19 (and_19_out, and_18_out, nor_4_out, nor_5_out);
  and and_20 (and_20_out, nor_1_out, nor_2_out, nor_3_out, nor_4_out);
  and and_21 (and_21_out, and_20_out, nor_5_out, nor_6_out);
  or or_1 (or_1_out, and_13_out, and_14_out);
  or or_2 (or_2_out, and_15_out, and_17_out);
  or or_3 (or_3_out, or_2_out, or_1_out);
  or or_4 (or_4_out, and_2_out, and_19_out);
  or or_5 (or_5_out, or_3_out, or_4_out);
  and and_22 (SF, or_5_out, in_13);
  and and_23 (ZF, and_21_out, in_13);
endmodule
