// Logisim project TEST.circ as structural Verilog: 1 circuit, main circuit main
module main (
  input  [5:0] A,
  input  [5:0] B,
  input  Habilitar,
  output SF,
  output ZF
);

  Comparador comparador_1 (.A(A), .B(B), .Hab(Habilitar), .SF(SF), .ZF(ZF));

  // Notes on the sheet:
  //   Comparador
endmodule
