// Logisim project Cero6b.circ as structural Verilog: 2 circuits, main circuit main
module main (
  input  [5:0] Entrada,
  output CF
);

  Cero6b cero6b_1 (.Entrada(Entrada), .CF(CF));
endmodule

module Cero6b (
  input  [5:0] Entrada,
  output CF
);

  nor nor_1 (CF, Entrada[0], Entrada[1], Entrada[2], Entrada[3], Entrada[4], Entrada[5]);

  // Notes on the sheet:
  //   NOR=1 cuando todos los bits de entrada son 0
endmodule
