// Logisim project Complemento2.circ as structural Verilog: 2 circuits, main circuit main
module main (
  input  [5:0] A,
  output Of,
  output [5:0] S
);

  // Probe on A
  CompA2 compa2_1 (.A(A), .Of(Of), .S(S));
  // Probe on S
endmodule

module CompA2 (
  input  [5:0] A,
  output Of,
  output [5:0] S
);

  wire [5:0] not_1_out, pull_resistor_1_node;

  not not_1 (not_1_out[0], A[0]);
  not not_2 (not_1_out[1], A[1]);
  not not_3 (not_1_out[2], A[2]);
  not not_4 (not_1_out[3], A[3]);
  not not_5 (not_1_out[4], A[4]);
  not not_6 (not_1_out[5], A[5]);
  Sumador6b sumador6b_1 (
    .A(not_1_out), .B({{5{pull_resistor_1_node[5]}}, pull_resistor_1_node[0]}),
    .Cin(pull_resistor_1_node[5]), .Of(Of), .S(S));
  Pull_Resistor #(.pull(1)) pull_resistor_1 (.node(pull_resistor_1_node[0]));
  Pull_Resistor pull_resistor_2 (.node(pull_resistor_1_node[5]));

  // Notes on the sheet:
  //   Se invierten los bits
  //   Se suma 1
endmodule
