// Logisim project Sumador6bits.circ as structural Verilog: 3 circuits, main circuit main
module main (
  input  [5:0] A,
  input  [5:0] B,
  input  Cin,
  output Of,
  output [5:0] S
);

  // Probe on A
  // Probe on B
  Sumador6b sumador6b_1 (.A(A), .B(B), .Cin(Cin), .Of(Of), .S(S));
  // Probe on S
endmodule

module Compr__OverFlow (
  input  Signo_A,
  input  Signo_B,
  input  Signo_S,
  output OverFlow
);

  wire xnor_1_out, xor_1_out;

  xnor xnor_1 (xnor_1_out, Signo_A, Signo_B);
  xor xor_1 (xor_1_out, Signo_B, Signo_S);
  and and_1 (OverFlow, xnor_1_out, xor_1_out);

  // Notes on the sheet:
  //   1 si A y B coinciden
  //   1 si B y S difieren
endmodule

module Sumador6b (
  input  [5:0] A,
  input  [5:0] B,
  input  Cin,
  output Of,
  output [5:0] S
);

  wire sumador1b_1_cout, sumador1b_2_cout, sumador1b_3_cout, sumador1b_4_cout, sumador1b_5_cout;

  Sumador1b sumador1b_1 (.A(A[0]), .B(B[0]), .Cin(Cin), .S(S[0]), .Cout(sumador1b_1_cout));
  Sumador1b sumador1b_2 (.A(A[1]), .B(B[1]), .Cin(sumador1b_1_cout), .S(S[1]), .Cout(sumador1b_2_cout));
  Sumador1b sumador1b_3 (.A(A[3]), .B(B[3]), .Cin(sumador1b_4_cout), .S(S[3]), .Cout(sumador1b_3_cout));
  Sumador1b sumador1b_4 (.A(A[2]), .B(B[2]), .Cin(sumador1b_2_cout), .S(S[2]), .Cout(sumador1b_4_cout));
  Sumador1b sumador1b_5 (.A(A[4]), .B(B[4]), .Cin(sumador1b_3_cout), .S(S[4]), .Cout(sumador1b_5_cout));
  Compr__OverFlow compr_overflow_1 (.Signo_A(A[5]), .Signo_B(B[5]), .Signo_S(S[5]), .OverFlow(Of));
  Sumador1b sumador1b_6 (.A(A[5]), .B(B[5]), .Cin(sumador1b_5_cout), .S(S[5]));  // open: Cout
endmodule
