// Logisim project 6bits.circ as structural Verilog: 4 circuits, main circuit main
module main (
  input  [5:0] A,
  input  Habilitar,
  output [5:0] Salida
);

  Habilitador6bits habilitador6bits_1 (.A(A), .Salida(Salida), .Habilitar(Habilitar));
endmodule

module Habilitador6bits (
  input  [5:0] A,
  input  Habilitar,
  output [5:0] Salida
);

  and and_1 (Salida[0], A[0], Habilitar);
  and and_2 (Salida[1], A[1], Habilitar);
  and and_3 (Salida[2], A[2], Habilitar);
  and and_4 (Salida[3], A[3], Habilitar);
  and and_5 (Salida[4], A[4], Habilitar);
  and and_6 (Salida[5], A[5], Habilitar);
endmodule

module Merge6bits (
  input  [5:0] A,
  input  [5:0] B,
  output [5:0] Salida
);

  or or_1 (Salida[0], A[0], B[0]);
  or or_2 (Salida[1], A[1], B[1]);
  or or_3 (Salida[2], A[2], B[2]);
  or or_4 (Salida[3], A[3], B[3]);
  or or_5 (Salida[4], A[4], B[4]);
  or or_6 (Salida[5], A[5], B[5]);
endmodule

module Merge7_Entradas (
  input  [5:0] And,
  input  [5:0] Or,
  input  [5:0] XOr,
  input  [5:0] Not,
  input  [5:0] ShL,
  input  [5:0] ShRL,
  input  [5:0] ShRA,
  output [5:0] out_8
);

  wire [5:0] merge6bits_1_salida, merge6bits_2_salida, merge6bits_3_salida, merge6bits_4_salida,
       merge6bits_5_salida;

  Merge6bits merge6bits_1 (.A(And), .B(Or), .Salida(merge6bits_1_salida));
  Merge6bits merge6bits_2 (.A(merge6bits_1_salida), .B(XOr), .Salida(merge6bits_2_salida));
  Merge6bits merge6bits_3 (.A(merge6bits_2_salida), .B(Not), .Salida(merge6bits_3_salida));
  Merge6bits merge6bits_4 (.A(merge6bits_3_salida), .B(ShL), .Salida(merge6bits_4_salida));
  Merge6bits merge6bits_5 (.A(merge6bits_4_salida), .B(ShRL), .Salida(merge6bits_5_salida));
  Merge6bits merge6bits_6 (.A(merge6bits_5_salida), .B(ShRA), .Salida(out_8));

  // Notes on the sheet:
  //   Merge de 6 bits en cascada
endmodule
