// Logisim project And.circ as structural Verilog: 2 circuits, main circuit main
module main (
  input  [5:0] A,
  input  [5:0] B,
  output [5:0] Salida
);

  And6bits and6bits_1 (.Salida(Salida), .A(A), .B(B));

  // Notes on the sheet:
  //   AND 6 bits
endmodule

module And6bits (
  input  [5:0] A,
  input  [5:0] B,
  output [5:0] Salida
);

  and and_1 (Salida[0], A[0], B[0]);
  and and_2 (Salida[1], A[1], B[1]);
  and and_3 (Salida[2], A[2], B[2]);
  and and_4 (Salida[3], A[3], B[3]);
  and and_5 (Salida[4], A[4], B[4]);
  and and_6 (Salida[5], A[5], B[5]);
endmodule
