// Logisim project Logico.circ as structural Verilog: 2 circuits, main circuit main
module main (
  input  [5:0] A,
  input  [5:0] B,
  input  [2:0] Funcion,
  input  Habilitar,
  output [5:0] Salida
);

  Logico logico_1 (.A(A), .B(B), .Control(Funcion), .Habilitador(Habilitar), .Salida(Salida));

  // Notes on the sheet:
  //   Selector y funciones
endmodule

module Logico (
  input  [5:0] A,
  input  [5:0] B,
  input  [2:0] Control,
  input  Habilitador,
  output [5:0] Salida
);

  wire and_1_out, and_2_out, and_3_out, and_4_out, and_5_out, and_6_out, and_7_out, and_8_out, and_9_out,
       nor_1_out, not_1_out, not_2_out, not_3_out, not_4_out, not_5_out;
  wire [5:0] and6bits_1_salida, habilitador6bits_1_salida, habilitador6bits_2_salida,
       habilitador6bits_3_salida, habilitador6bits_4_salida, habilitador6bits_5_salida,
       habilitador6bits_6_salida, habilitador6bits_7_salida, merge7_entradas_1_out_8, not_6_bits_1_salida,
       or6bits_1_salida, shiftleft_1_salida, shiftrighta_1_salida, shiftrightl_1_salida, xor6bits_1_salida;

  not not_1 (not_1_out, Control[0]);
  nor nor_1 (nor_1_out, Control[1], Control[2]);
  not not_2 (not_2_out, Control[0]);
  not not_3 (not_3_out, Control[2]);
  and and_1 (and_1_out, not_3_out, Control[1]);
  not not_4 (not_4_out, Control[0]);
  and and_2 (and_2_out, Control[2], not_5_out);
  not not_5 (not_5_out, Control[1]);
  and and_3 (and_3_out, Control[1], Control[2]);
  And6bits and6bits_1 (.Salida(and6bits_1_salida), .A(A), .B(B));
  Or6bits or6bits_1 (.Salida(or6bits_1_salida), .A(A), .B(B));
  XOr6bits xor6bits_1 (.Salida(xor6bits_1_salida), .A(A), .B(B));
  NOT_6_bits not_6_bits_1 (.A(A), .Salida(not_6_bits_1_salida));
  ShiftLeft shiftleft_1 (.A(A), .Salida(shiftleft_1_salida));
  ShiftRightL shiftrightl_1 (.A(A), .Salida(shiftrightl_1_salida));
  ShiftRightA shiftrighta_1 (.A(A), .Salida(shiftrighta_1_salida));
  and and_4 (and_4_out, not_1_out, nor_1_out);
  and and_5 (and_5_out, Control[0], nor_1_out);
  and and_6 (and_6_out, not_2_out, and_1_out);
  and and_7 (and_7_out, Control[0], and_1_out);
  and and_8 (and_8_out, not_4_out, and_2_out);
  and and_9 (and_9_out, Control[0], and_2_out);
  Habilitador6bits habilitador6bits_1 (
    .A(and6bits_1_salida), .Salida(habilitador6bits_1_salida), .Habilitar(and_4_out));
  Habilitador6bits habilitador6bits_2 (.A(or6bits_1_salida), .Salida(habilitador6bits_2_salida), .Habilitar(and_5_out));
  Habilitador6bits habilitador6bits_3 (
    .A(xor6bits_1_salida), .Salida(habilitador6bits_3_salida), .Habilitar(and_6_out));
  Habilitador6bits habilitador6bits_4 (
    .A(not_6_bits_1_salida), .Salida(habilitador6bits_4_salida), .Habilitar(and_7_out));
  Habilitador6bits habilitador6bits_5 (
    .A(shiftleft_1_salida), .Salida(habilitador6bits_5_salida), .Habilitar(and_8_out));
  Habilitador6bits habilitador6bits_6 (
    .A(shiftrightl_1_salida), .Salida(habilitador6bits_6_salida), .Habilitar(and_9_out));
  Habilitador6bits habilitador6bits_7 (
    .A(shiftrighta_1_salida), .Salida(habilitador6bits_7_salida), .Habilitar(and_3_out));
  Merge7_Entradas merge7_entradas_1 (
    .And(habilitador6bits_1_salida), .Or(habilitador6bits_2_salida), .XOr(habilitador6bits_3_salida),
    .Not(habilitador6bits_4_salida), .ShL(habilitador6bits_5_salida), .ShRL(habilitador6bits_6_salida),
    .ShRA(habilitador6bits_7_salida), .out_8(merge7_entradas_1_out_8));
  Habilitador6bits habilitador6bits_8 (.A(merge7_entradas_1_out_8), .Salida(Salida), .Habilitar(Habilitador));

  // Notes on the sheet:
  //   Selector de función
  //   Funciones
endmodule
