// Logisim project Not.circ as structural Verilog: 2 circuits, main circuit main
module main (
  input  [5:0] A,
  output [5:0] Salida
);

  NOT_6_bits not_6_bits_1 (.A(A), .Salida(Salida));

  // Notes on the sheet:
  //   NOT 6 bits
endmodule

module NOT_6_bits (
  input  [5:0] A,
  output [5:0] Salida
);

  not not_1 (Salida[0], A[0]);
  not not_2 (Salida[1], A[1]);
  not not_3 (Salida[2], A[2]);
  not not_4 (Salida[3], A[3]);
  not not_5 (Salida[4], A[4]);
  not not_6 (Salida[5], A[5]);
endmodule
