// Logisim project Or.circ as structural Verilog: 2 circuits, main circuit main
module main (
  input  [5:0] A,
  input  [5:0] B,
  output [5:0] Salida
);

  Or6bits or6bits_1 (.Salida(Salida), .A(A), .B(B));

  // Notes on the sheet:
  //   OR 6 bits
endmodule

module Or6bits (
  input  [5:0] A,
  input  [5:0] B,
  output [5:0] Salida
);

  or or_1 (Salida[0], A[0], B[0]);
  or or_2 (Salida[1], A[1], B[1]);
  or or_3 (Salida[2], A[2], B[2]);
  or or_4 (Salida[3], A[3], B[3]);
  or or_5 (Salida[4], A[4], B[4]);
  or or_6 (Salida[5], A[5], B[5]);
endmodule
