// Logisim project ShL.circ as structural Verilog: 2 circuits, main circuit main
module main (
  input  [5:0] A,
  output [5:0] Salida
);

  ShiftLeft shiftleft_1 (.A(A), .Salida(Salida));

  // Notes on the sheet:
  //   Corrimiento a la izquierda
endmodule

module ShiftLeft (
  input  [5:0] A,
  output [5:0] Salida
);

  Pull_Resistor pull_resistor_1 (.node(Salida[0]));

  assign Salida[5:1] = A[4:0];
endmodule
