// Logisim project ShRA.circ as structural Verilog: 2 circuits, main circuit main
module main (
  input  [5:0] A,
  output [5:0] Salida
);

  ShiftRightA shiftrighta_1 (.A(A), .Salida(Salida));

  // Notes on the sheet:
  //   Corrimiento derecho aritmético
endmodule

module ShiftRightA (
  input  [5:0] A,
  output [5:0] Salida
);


  assign Salida = {{2{A[5]}}, A[4:1]};
endmodule
