// Logisim project ShRL.circ as structural Verilog: 2 circuits, main circuit main
module main (
  input  [5:0] A,
  output [5:0] Salida
);

  ShiftRightL shiftrightl_1 (.A(A), .Salida(Salida));

  // Notes on the sheet:
  //   Corrimiento derecho lógico
endmodule

module ShiftRightL (
  input  [5:0] A,
  output [5:0] Salida
);

  Pull_Resistor pull_resistor_1 (.node(Salida[5]));

  assign Salida[4:0] = A[5:1];
endmodule
