// Logisim project TEST.circ as structural Verilog: 1 circuit, main circuit main
module main (
  input  [5:0] A,
  input  [5:0] B,
  input  [2:0] Funcion,
  input  Habilitar,
  output [5:0] Salida
);

  Logico logico_1 (.A(A), .B(B), .Control(Funcion), .Habilitador(Habilitar), .Salida(Salida));

  // Notes on the sheet:
  //   Selector y funciones
endmodule
