// Logisim project XOr.circ as structural Verilog: 2 circuits, main circuit main
module main (
  input  [5:0] A,
  input  [5:0] B,
  output [5:0] Salida
);

  XOr6bits xor6bits_1 (.Salida(Salida), .A(A), .B(B));

  // Notes on the sheet:
  //   XOR 6 bits
endmodule

module XOr6bits (
  input  [5:0] A,
  input  [5:0] B,
  output [5:0] Salida
);

  xor xor_1 (Salida[0], A[0], B[0]);
  xor xor_2 (Salida[1], A[1], B[1]);
  xor xor_3 (Salida[2], A[2], B[2]);
  xor xor_4 (Salida[3], A[3], B[3]);
  xor xor_5 (Salida[4], A[4], B[4]);
  xor xor_6 (Salida[5], A[5], B[5]);
endmodule
