// Logisim project 10 bits.circ as structural Verilog
module A10bits (
  input  [4:0] in_1,
  output [9:0] out_2
);

  Pull_Resistor pull_resistor_1 (.node(out_2[9]));

  assign out_2[8:0] = {{4{out_2[9]}}, in_1};
endmodule

module Sumador10bits (
  input  [9:0] Entrada_A,
  input  [9:0] Entrada_B,
  input  Cin,
  output Cout,
  output [9:0] Salida
);

  wire sumador1b_1_cout, sumador1b_2_cout, sumador1b_3_cout, sumador1b_4_cout, sumador1b_5_cout,
       sumador1b_6_cout, sumador1b_7_cout, sumador1b_8_cout, sumador1b_10_cout;

  Sumador1b sumador1b_1 (
    .A(Entrada_A[1]), .B(Entrada_B[1]), .Cin(sumador1b_2_cout), .S(Salida[1]), .Cout(sumador1b_1_cout));
  Sumador1b sumador1b_2 (.A(Entrada_A[0]), .B(Entrada_B[0]), .Cin(Cin), .S(Salida[0]), .Cout(sumador1b_2_cout));
  Sumador1b sumador1b_3 (
    .A(Entrada_A[3]), .B(Entrada_B[3]), .Cin(sumador1b_4_cout), .S(Salida[3]), .Cout(sumador1b_3_cout));
  Sumador1b sumador1b_4 (
    .A(Entrada_A[2]), .B(Entrada_B[2]), .Cin(sumador1b_1_cout), .S(Salida[2]), .Cout(sumador1b_4_cout));
  Sumador1b sumador1b_5 (
    .A(Entrada_A[4]), .B(Entrada_B[4]), .Cin(sumador1b_3_cout), .S(Salida[4]), .Cout(sumador1b_5_cout));
  Sumador1b sumador1b_6 (
    .A(Entrada_A[6]), .B(Entrada_B[6]), .Cin(sumador1b_7_cout), .S(Salida[6]), .Cout(sumador1b_6_cout));
  Sumador1b sumador1b_7 (
    .A(Entrada_A[5]), .B(Entrada_B[5]), .Cin(sumador1b_5_cout), .S(Salida[5]), .Cout(sumador1b_7_cout));
  Sumador1b sumador1b_8 (
    .A(Entrada_A[7]), .B(Entrada_B[7]), .Cin(sumador1b_6_cout), .S(Salida[7]), .Cout(sumador1b_8_cout));
  Sumador1b sumador1b_9 (.A(Entrada_A[9]), .B(Entrada_B[9]), .Cin(sumador1b_10_cout), .S(Salida[9]), .Cout(Cout));
  Sumador1b sumador1b_10 (
    .A(Entrada_A[8]), .B(Entrada_B[8]), .Cin(sumador1b_8_cout), .S(Salida[8]), .Cout(sumador1b_10_cout));
endmodule

module ShiftLeft10bits (
  input  [9:0] in_1,
  output [9:0] out_2
);

  Pull_Resistor pull_resistor_1 (.node(out_2[0]));

  assign out_2[9:1] = in_1[8:0];
endmodule

module Selector10bits (
  input  [9:0] Entrada,
  input  Habilitado,
  output [9:0] Salida
);

  and and_1 (Salida[0], Entrada[0], Habilitado);
  and and_2 (Salida[1], Entrada[1], Habilitado);
  and and_3 (Salida[2], Entrada[2], Habilitado);
  and and_4 (Salida[3], Entrada[3], Habilitado);
  and and_5 (Salida[4], Entrada[4], Habilitado);
  and and_6 (Salida[5], Entrada[5], Habilitado);
  and and_7 (Salida[6], Entrada[6], Habilitado);
  and and_8 (Salida[7], Entrada[7], Habilitado);
  and and_9 (Salida[8], Entrada[8], Habilitado);
  and and_10 (Salida[9], Entrada[9], Habilitado);
endmodule

module Merge10bits (
  input  [9:0] A,
  input  [9:0] B,
  output [9:0] out_3
);

  or or_1 (out_3[0], A[0], B[0]);
  or or_2 (out_3[1], A[1], B[1]);
  or or_3 (out_3[2], A[2], B[2]);
  or or_4 (out_3[3], A[3], B[3]);
  or or_5 (out_3[4], A[4], B[4]);
  or or_6 (out_3[5], A[5], B[5]);
  or or_7 (out_3[6], A[6], B[6]);
  or or_8 (out_3[7], A[7], B[7]);
  or or_9 (out_3[8], A[8], B[8]);
  or or_10 (out_3[9], A[9], B[9]);
endmodule

module CompA2_10bits (
  input  [9:0] Entrada,
  output [9:0] Salida,
  output CF
);

  wire [9:0] not_1_out;

  not not_1 (not_1_out[0], Entrada[0]);
  not not_2 (not_1_out[1], Entrada[1]);
  not not_3 (not_1_out[2], Entrada[2]);
  not not_4 (not_1_out[3], Entrada[3]);
  not not_5 (not_1_out[4], Entrada[4]);
  not not_6 (not_1_out[5], Entrada[5]);
  not not_7 (not_1_out[6], Entrada[6]);
  not not_8 (not_1_out[7], Entrada[7]);
  not not_9 (not_1_out[8], Entrada[8]);
  not not_10 (not_1_out[9], Entrada[9]);
  Sumador10bits sumador10bits_1 (.Entrada_A(not_1_out), .Entrada_B(10'h1), .Cin(1'b0), .Cout(CF), .Salida(Salida));
endmodule
