// Logisim project 5bits.circ as structural Verilog: 3 circuits, main circuit main
module main (
  input  [4:0] A,
  input  in_2,
  input  [4:0] A_2,
  input  [4:0] B,
  output [4:0] Salida,
  output [4:0] Salida_2
);

  Habilitador5bits habilitador5bits_1 (.Entrada(A), .Hab(in_2), .Salida(Salida));
  Merge5bits merge5bits_1 (.A(A_2), .B(B), .S(Salida_2));

  // Notes on the sheet:
  //   Habilitar 5 bits
  //   Merge 5 bits
endmodule

module Habilitador5bits (
  input  [4:0] Entrada,
  input  Hab,
  output [4:0] Salida
);

  and and_1 (Salida[0], Entrada[0], Hab);
  and and_2 (Salida[1], Entrada[1], Hab);
  and and_3 (Salida[2], Entrada[2], Hab);
  and and_4 (Salida[3], Entrada[3], Hab);
  and and_5 (Salida[4], Entrada[4], Hab);
endmodule

module Merge5bits (
  input  [4:0] A,
  input  [4:0] B,
  output [4:0] S
);

  or or_1 (S[0], A[0], B[0]);
  or or_2 (S[1], A[1], B[1]);
  or or_3 (S[2], A[2], B[2]);
  or or_4 (S[3], A[3], B[3]);
  or or_5 (S[4], A[4], B[4]);
endmodule
