// Logisim project Multiplicador.circ as structural Verilog: 5 circuits, main circuit main
module main (
  input  [5:0] A,
  input  [5:0] B,
  input  Hab,
  output CF,
  output SF,
  output [11:0] Salida
);

  // Probe on A
  // Probe on B
  Multiplicador multiplicador_1 (.A(A), .B(B), .Hab(Hab), .ZF(CF), .SF(SF), .Salida(Salida));
  // Probe on Salida
endmodule

module Multiplicador (
  input  [5:0] A,
  input  [5:0] B,
  input  Hab,
  output ZF,
  output SF,
  output [11:0] Salida
);

  wire cero12bits_1_zf, csigno_1_ss, not_1_out, pull_resistor_1_node, sumador10bits_1_cout,
       sumador10bits_2_cout, sumador10bits_3_cout;
  wire [4:0] habilitador5bits_1_salida, habilitador5bits_2_salida, habilitador5bits_3_salida,
       habilitador5bits_4_salida, habilitador5bits_5_salida, valorabsoluto_1_salida, valorabsoluto_2_salida;
  wire [9:0] a10bits_1_out_2, a10bits_2_out_2, a10bits_3_out_2, a10bits_4_out_2, a10bits_5_out_2,
       compa2_10bits_1_salida, merge10bits_1_out_3, selector10bits_1_salida, selector10bits_2_salida,
       shiftleft10bits_1_out_2, shiftleft10bits_2_out_2, shiftleft10bits_3_out_2, shiftleft10bits_4_out_2,
       shiftleft10bits_5_out_2, shiftleft10bits_6_out_2, shiftleft10bits_7_out_2, shiftleft10bits_8_out_2,
       shiftleft10bits_9_out_2, shiftleft10bits_10_out_2, sumador10bits_1_salida, sumador10bits_2_salida,
       sumador10bits_3_salida, sumador10bits_4_salida;

  // Probe on A
  // Probe on B
  ValorAbsoluto valorabsoluto_1 (.Entrada(A), .Salida(valorabsoluto_1_salida));  // open: OF
  ValorAbsoluto valorabsoluto_2 (.Entrada(B), .Salida(valorabsoluto_2_salida));  // open: OF
  CSigno csigno_1 (.sA(A[5]), .sB(B[5]), .sS(csigno_1_ss));
  Habilitador5bits habilitador5bits_1 (
    .Entrada(valorabsoluto_1_salida), .Hab(valorabsoluto_2_salida[0]), .Salida(habilitador5bits_1_salida));
  Habilitador5bits habilitador5bits_2 (
    .Entrada(valorabsoluto_1_salida), .Hab(valorabsoluto_2_salida[1]), .Salida(habilitador5bits_2_salida));
  Habilitador5bits habilitador5bits_3 (
    .Entrada(valorabsoluto_1_salida), .Hab(valorabsoluto_2_salida[2]), .Salida(habilitador5bits_3_salida));
  Habilitador5bits habilitador5bits_4 (
    .Entrada(valorabsoluto_1_salida), .Hab(valorabsoluto_2_salida[3]), .Salida(habilitador5bits_4_salida));
  Habilitador5bits habilitador5bits_5 (
    .Entrada(valorabsoluto_1_salida), .Hab(valorabsoluto_2_salida[4]), .Salida(habilitador5bits_5_salida));
  Pull_Resistor pull_resistor_1 (.node(pull_resistor_1_node));
  A10bits a10bits_1 (.in_1(habilitador5bits_1_salida), .out_2(a10bits_1_out_2));
  A10bits a10bits_2 (.in_1(habilitador5bits_2_salida), .out_2(a10bits_2_out_2));
  ShiftLeft10bits shiftleft10bits_1 (.in_1(a10bits_2_out_2), .out_2(shiftleft10bits_1_out_2));
  A10bits a10bits_3 (.in_1(habilitador5bits_3_salida), .out_2(a10bits_3_out_2));
  ShiftLeft10bits shiftleft10bits_2 (.in_1(a10bits_3_out_2), .out_2(shiftleft10bits_2_out_2));
  ShiftLeft10bits shiftleft10bits_3 (.in_1(a10bits_4_out_2), .out_2(shiftleft10bits_3_out_2));
  A10bits a10bits_4 (.in_1(habilitador5bits_4_salida), .out_2(a10bits_4_out_2));
  A10bits a10bits_5 (.in_1(habilitador5bits_5_salida), .out_2(a10bits_5_out_2));
  ShiftLeft10bits shiftleft10bits_4 (.in_1(a10bits_5_out_2), .out_2(shiftleft10bits_4_out_2));
  Sumador10bits sumador10bits_1 (
    .Entrada_A(a10bits_1_out_2), .Entrada_B(shiftleft10bits_1_out_2), .Cin(pull_resistor_1_node),
    .Cout(sumador10bits_1_cout), .Salida(sumador10bits_1_salida));
  ShiftLeft10bits shiftleft10bits_5 (.in_1(shiftleft10bits_2_out_2), .out_2(shiftleft10bits_5_out_2));
  ShiftLeft10bits shiftleft10bits_6 (.in_1(shiftleft10bits_3_out_2), .out_2(shiftleft10bits_6_out_2));
  ShiftLeft10bits shiftleft10bits_7 (.in_1(shiftleft10bits_6_out_2), .out_2(shiftleft10bits_7_out_2));
  ShiftLeft10bits shiftleft10bits_8 (.in_1(shiftleft10bits_9_out_2), .out_2(shiftleft10bits_8_out_2));
  ShiftLeft10bits shiftleft10bits_9 (.in_1(shiftleft10bits_4_out_2), .out_2(shiftleft10bits_9_out_2));
  Sumador10bits sumador10bits_2 (
    .Entrada_A(shiftleft10bits_5_out_2), .Entrada_B(sumador10bits_1_salida), .Cin(sumador10bits_1_cout),
    .Cout(sumador10bits_2_cout), .Salida(sumador10bits_2_salida));
  ShiftLeft10bits shiftleft10bits_10 (.in_1(shiftleft10bits_8_out_2), .out_2(shiftleft10bits_10_out_2));
  Sumador10bits sumador10bits_3 (
    .Entrada_A(sumador10bits_2_salida), .Entrada_B(shiftleft10bits_7_out_2), .Cin(sumador10bits_2_cout),
    .Cout(sumador10bits_3_cout), .Salida(sumador10bits_3_salida));
  Sumador10bits sumador10bits_4 (
    .Entrada_A(sumador10bits_3_salida), .Entrada_B(shiftleft10bits_10_out_2), .Cin(sumador10bits_3_cout),
    .Salida(sumador10bits_4_salida));  // open: Cout
  CompA2_10bits compa2_10bits_1 (.Entrada(sumador10bits_4_salida), .Salida(compa2_10bits_1_salida));  // open: CF
  Selector10bits selector10bits_1 (
    .Entrada(compa2_10bits_1_salida), .Habilitado(csigno_1_ss), .Salida(selector10bits_1_salida));
  Merge10bits merge10bits_1 (.A(selector10bits_1_salida), .B(selector10bits_2_salida), .out_3(merge10bits_1_out_3));
  Selector10bits selector10bits_2 (
    .Entrada(sumador10bits_4_salida), .Habilitado(not_1_out), .Salida(selector10bits_2_salida));
  not not_1 (not_1_out, csigno_1_ss);
  and and_1 (SF, csigno_1_ss, Hab);
  Selector10bits selector10bits_3 (.Entrada(merge10bits_1_out_3), .Habilitado(Hab), .Salida(Salida[9:0]));
  and and_2 (Salida[11], csigno_1_ss, Hab);
  Cero12bits cero12bits_1 (.Entrada({{2{Salida[11]}}, Salida[9:0]}), .ZF(cero12bits_1_zf));
  and and_3 (ZF, cero12bits_1_zf, Hab);
  // Probe on {{2{Salida[11]}}, Salida[9:0]}

  assign Salida[10] = Salida[11];

  // Notes on the sheet:
  //   Obt. Signo
  //   Mult. por 0 o 1
  //   A 10 bits
  //   --------- LeftShifters -------
  //   Sumas
  //   Comp. a 2 si es necesario
  //   Habilitar si Hab=1
endmodule

module CSigno (
  input  sA,
  input  sB,
  output sS
);

  xor xor_1 (sS, sA, sB);
endmodule

module ValorAbsoluto (
  input  [5:0] Entrada,
  output OF,
  output [4:0] Salida
);

  wire not_1_out;
  wire [4:0] habilitador5bits_1_salida, habilitador5bits_2_salida;
  wire [5:0] compa2_1_s;

  CompA2 compa2_1 (.A(Entrada), .Of(OF), .S(compa2_1_s));
  Habilitador5bits habilitador5bits_1 (.Entrada(compa2_1_s[4:0]), .Hab(Entrada[5]), .Salida(habilitador5bits_1_salida));
  Habilitador5bits habilitador5bits_2 (.Entrada(Entrada[4:0]), .Hab(not_1_out), .Salida(habilitador5bits_2_salida));
  not not_1 (not_1_out, Entrada[5]);
  Merge5bits merge5bits_1 (.A(habilitador5bits_1_salida), .B(habilitador5bits_2_salida), .S(Salida));
endmodule

module Cero12bits (
  input  [11:0] Entrada,
  output ZF
);

  nor nor_1 (ZF, Entrada[0], Entrada[1], Entrada[2], Entrada[3], Entrada[4], Entrada[5], Entrada[6], Entrada[7], Entrada[8], Entrada[9], Entrada[10], Entrada[11]);
endmodule
