// Logisim project TEST.circ as structural Verilog: 1 circuit, main circuit main
module main (
  input  [5:0] A,
  input  [5:0] B,
  input  Hab,
  output CF,
  output SF,
  output [11:0] Salida
);

  // Probe on A
  // Probe on B
  Multiplicador multiplicador_1 (.A(A), .B(B), .Hab(Hab), .ZF(CF), .SF(SF), .Salida(Salida));
  // Probe on Salida
endmodule
