// Logisim project Sum-Rest.circ as structural Verilog: 4 circuits, main circuit main
module main (
  input  [5:0] A,
  input  [5:0] B,
  input  Ctrl,
  input  Cin,
  input  Hab,
  output [5:0] S,
  output ZF,
  output CF,
  output SF
);

  // Probe on A
  // Probe on B
  // Probe on S
  Sumador_Restador sumador_restador_1 (
    .A(A), .B(B), .Ctrl(Ctrl), .Cin(Cin), .Hab(Hab), .S(S), .ZF(ZF), .CF(CF), .SF(SF));

  // Notes on the sheet:
  //   Entradas A y B
  //   Crtl 0: Suma / 1: Resta
  //   Cin = Acarreo de entrada
  //   Hab=Habilitar circuito
endmodule

module Sumador_Restador (
  input  [5:0] A,
  input  [5:0] B,
  input  Ctrl,
  input  Cin,
  input  Hab,
  output [5:0] S,
  output ZF,
  output CF,
  output SF
);

  wire and_1_out, cero6b_1_cf, compa2_1_of, not_1_out, sumador6b_1_of;
  wire [5:0] compa2_1_s, mezclador_1_out_3, selector_1_salida, selector_2_salida, sumador6b_1_s;

  CompA2 compa2_1 (.A(B), .Of(compa2_1_of), .S(compa2_1_s));
  Selector selector_1 (.Entrada(B), .Ctrl(not_1_out), .Salida(selector_1_salida));
  not not_1 (not_1_out, Ctrl);
  Selector selector_2 (.Entrada(compa2_1_s), .Ctrl(Ctrl), .Salida(selector_2_salida));
  Mezclador mezclador_1 (.A(selector_1_salida), .B(selector_2_salida), .out_3(mezclador_1_out_3));
  Sumador6b sumador6b_1 (.A(A), .B(mezclador_1_out_3), .Cin(Cin), .Of(sumador6b_1_of), .S(sumador6b_1_s));
  Selector selector_3 (.Entrada(sumador6b_1_s), .Ctrl(Hab), .Salida(S));
  Cero6b cero6b_1 (.Entrada(S), .CF(cero6b_1_cf));
  and and_1 (and_1_out, sumador6b_1_of, Hab, compa2_1_of);
  and and_2 (ZF, cero6b_1_cf, Hab);
  and and_3 (CF, and_1_out, Hab);
  and and_4 (SF, S[5], Hab);

  // Notes on the sheet:
  //   Entradas
  //   Selecciono B o -B
  //   Suma
endmodule

module Selector (
  input  [5:0] Entrada,
  input  Ctrl,
  output [5:0] Salida
);

  and and_1 (Salida[5], Ctrl, Entrada[5]);
  and and_2 (Salida[4], Ctrl, Entrada[4]);
  and and_3 (Salida[3], Ctrl, Entrada[3]);
  and and_4 (Salida[2], Ctrl, Entrada[2]);
  and and_5 (Salida[1], Ctrl, Entrada[1]);
  and and_6 (Salida[0], Ctrl, Entrada[0]);

  // Notes on the sheet:
  //   S=Entrada cuando Ctrl=1
endmodule

module Mezclador (
  input  [5:0] A,
  input  [5:0] B,
  output [5:0] out_3
);

  or or_1 (out_3[0], A[0], B[0]);
  or or_2 (out_3[1], A[1], B[1]);
  or or_3 (out_3[2], A[2], B[2]);
  or or_4 (out_3[3], A[3], B[3]);
  or or_5 (out_3[4], A[4], B[4]);
  or or_6 (out_3[5], A[5], B[5]);

  // Notes on the sheet:
  //   Merge
endmodule
