// Logisim project TEST.circ as structural Verilog: 1 circuit, main circuit main
module main (
  input  [5:0] A,
  input  [5:0] B,
  input  Ctrl,
  input  Cin,
  input  Hab,
  output [5:0] S,
  output ZF,
  output CF,
  output SF
);

  // Probe on A
  // Probe on B
  // Probe on S
  Sumador_Restador sumador_restador_1 (
    .A(A), .B(B), .Ctrl(Ctrl), .Cin(Cin), .Hab(Hab), .S(S), .ZF(ZF), .CF(CF), .SF(SF));

  // Notes on the sheet:
  //   Entradas A y B
  //   Crtl 0: Suma / 1: Resta
  //   Cin = Acarreo de entrada
  //   Hab=Habilitar circuito
endmodule
